// Logisim project CPU.circ as structural Verilog: 9 circuits, main circuit main
module main (
);


  // Notes on the sheet:
  //   7.JZ 0X31
  //   9.JNZ 0X33
  //   10.JNC 0X34
  //   0.LOD 0x10
  //   1.STO 0x11
  //   2.ADD 0X20
  //   3.SUB 0X21
  //   4.ADC 0X22
  //   5.SBB 0X23
  //   6.JMP 0X30
  //   8.JC 0X32
  //   11.HLT 0XFF
endmodule

module ALU1Bit (
  input  SUM,
  input  AND,
  input  OR,
  input  cin,
  input  A_INV,
  input  B_INV,
  input  A,
  input  B,
  output out_9,
  output cout
);

  wire adder_1_out, and_1_out, or_1_out, xor_1_out, xor_2_out;

  xor xor_1 (xor_1_out, A, A_INV);
  xor xor_2 (xor_2_out, B, B_INV);
  Adder #(.width(1)) adder_1 (.a(xor_1_out), .b(xor_2_out), .out(adder_1_out), .cin(cin), .cout(cout));
  and and_1 (and_1_out, xor_1_out, xor_2_out);
  or or_1 (or_1_out, xor_1_out, xor_2_out);
  assign out_9 = SUM ? adder_1_out : 1'bz;  // Controlled_Buffer controlled_buffer_1
  assign out_9 = AND ? and_1_out : 1'bz;  // Controlled_Buffer controlled_buffer_2
  assign out_9 = OR ? or_1_out : 1'bz;  // Controlled_Buffer controlled_buffer_3
endmodule

module ALU8BIT (
  input  [7:0] in_1,
  input  [7:0] in_2,
  input  in_3,
  input  in_4,
  input  in_5,
  input  in_6,
  input  in_7,
  input  in_8,
  output out_9,
  output out_10,
  output out_11,
  output out_12,
  output [7:0] out_13
);

  wire alu1bit_2_cout, alu1bit_3_cout, alu1bit_4_cout, alu1bit_5_cout, alu1bit_6_cout, alu1bit_7_cout,
       alu1bit_8_cout;

  ALU1Bit alu1bit_1 (
    .A(in_1[7]), .B(in_2[7]), .out_9(out_10), .A_INV(in_3), .B_INV(in_4), .cin(alu1bit_2_cout), .SUM(in_6),
    .AND(in_7), .OR(in_8), .cout(out_9));
  ALU1Bit alu1bit_2 (
    .A(in_1[6]), .B(in_2[6]), .out_9(out_13[6]), .A_INV(in_3), .B_INV(in_4), .cin(alu1bit_3_cout),
    .SUM(in_6), .AND(in_7), .OR(in_8), .cout(alu1bit_2_cout));
  ALU1Bit alu1bit_3 (
    .A(in_1[5]), .B(in_2[5]), .out_9(out_13[5]), .A_INV(in_3), .B_INV(in_4), .cin(alu1bit_4_cout),
    .SUM(in_6), .AND(in_7), .OR(in_8), .cout(alu1bit_3_cout));
  ALU1Bit alu1bit_4 (
    .A(in_1[4]), .B(in_2[4]), .out_9(out_13[4]), .A_INV(in_3), .B_INV(in_4), .cin(alu1bit_5_cout),
    .SUM(in_6), .AND(in_7), .OR(in_8), .cout(alu1bit_4_cout));
  ALU1Bit alu1bit_5 (
    .A(in_1[3]), .B(in_2[3]), .out_9(out_13[3]), .A_INV(in_3), .B_INV(in_4), .cin(alu1bit_6_cout),
    .SUM(in_6), .AND(in_7), .OR(in_8), .cout(alu1bit_5_cout));
  ALU1Bit alu1bit_6 (
    .A(in_1[2]), .B(in_2[2]), .out_9(out_13[2]), .A_INV(in_3), .B_INV(in_4), .cin(alu1bit_7_cout),
    .SUM(in_6), .AND(in_7), .OR(in_8), .cout(alu1bit_6_cout));
  ALU1Bit alu1bit_7 (
    .A(in_1[1]), .B(in_2[1]), .out_9(out_13[1]), .A_INV(in_3), .B_INV(in_4), .cin(alu1bit_8_cout),
    .SUM(in_6), .AND(in_7), .OR(in_8), .cout(alu1bit_7_cout));
  ALU1Bit alu1bit_8 (
    .A(in_1[0]), .B(in_2[0]), .out_9(out_13[0]), .A_INV(in_3), .B_INV(in_4), .cin(in_5), .SUM(in_6),
    .AND(in_7), .OR(in_8), .cout(alu1bit_8_cout));
  xor xor_1 (out_11, out_9, alu1bit_2_cout);
  nor nor_1 (out_12, out_13[0], out_13[1], out_13[2], out_13[3], out_13[4], out_13[5], out_13[6], out_10);

  assign out_13[7] = out_10;
endmodule

module CU (
  input  in_1,
  input  [3:0] in_2,
  output out_3,
  output out_4,
  output out_5,
  output out_6,
  output out_7,
  output out_8,
  output out_9,
  output out_10,
  output out_11,
  output out_12,
  output out_13,
  output out_14,
  output out_15,
  output out_16,
  output out_17,
  output out_18,
  output out_19,
  output out_20,
  output [3:0] out_21,
  output out_22,
  output out_23,
  output out_24,
  output out_25,
  output out_26,
  output out_27,
  output out_28,
  output out_29,
  output out_30,
  output out_31,
  output out_32,
  output out_33,
  output out_34,
  output out_35
);

  wire not_1_out;
  wire [2:0] counter_1_q;
  wire [29:21] rom_1_data;

  Counter #(.width(3), .max('h7)) counter_1 (.clk(not_1_out), .Q(counter_1_q));  // open: clr, load, up, count, D, carry
  not not_1 (not_1_out, in_1);
  Register #(.width(4)) register_1 (.D(in_2), .en(out_34), .clk(not_1_out), .Q(out_21));  // open: clr
  ROM #(.addrWidth(7), .dataWidth(32)) rom_1 (
    .addr({out_21, counter_1_q}),
    .data({out_35, out_34, rom_1_data, out_24, out_23, out_22, out_20, out_19, out_18, out_17, out_16, out_15, out_14, out_13, out_12, out_11, out_10, out_9, out_8, out_7, out_6, out_5, out_4, out_3}));

  // Notes on the sheet:
  //   contents of rom_1 (hex, n*v repeats v):
  //   40000012 80003 40080003 8000b 80021 0 0 0 40000012 80003 40080003 8000b a0001 19*0 40000012 80003
  //   40080003 8000b 8400 10020 0 0 40000012 80003 40080003 8000b 8700 10020 26*0 40000012 80003 40080003
  //   8000b 8800 10020 0 0 40000012 80003 40080003 8000b 9000 10020 34*0 8*80000000
endmodule

module CPU (
  input  in_1,
  input  in_2
);

  wire AND, AR_OE, AR_WE, BR_OE, BR_WE, buffer_1_out, button_1_out, cin, clk, controlled_buffer_1_out,
       disp_board_1_out_2, disp_board_1_out_3, disp_board_1_out_4, disp_board_1_out_5, disp_board_1_out_6,
       disp_board_1_out_7, disp_board_1_out_8, disp_board_1_out_9, disp_board_1_out_10, disp_board_1_out_11,
       disp_board_1_out_12, disp_board_1_out_13, disp_board_1_out_14, disp_board_1_out_15,
       disp_board_1_out_16, disp_board_1_out_17, disp_board_1_out_18, disp_board_1_out_19,
       disp_board_1_out_20, disp_board_1_out_21, disp_board_1_out_22, disp_board_1_out_23,
       disp_board_1_out_24, disp_board_1_out_25, ER_OE, ER_WE, FLG_OE, FLG_WE, HLT, INV_A, INV_B, IR_OE,
       IR_WE, MAR_OB, MAR_OE, MAR_WE, OPR_WE, OR, OUT_WE, PC_LODE, PC_OE, PC_WE, RAM_OE, RAM_WE, SUM;
  wire [1:0] alu8bit_1_out_11, FLGR_O;
  wire [2:0] counter_2_q;
  wire [3:0] controlled_buffer_5_out, controlled_buffer_5_out_2, controlled_buffer_11_out, OPCODE_REG_q,
       pgmctr, register_6_q;
  wire [7:0] alu8bit_1_out_13, controlled_buffer_2_out, IR_q, ram_1_dout, register_1_q, register_2_q,
       register_4_q, register_5_q;
  wire [29:25] rom_1_data;

  Button button_1 (.out(button_1_out));
  Clock clock_1 (.in_1(in_1), .in_3(HLT), .out_4(clk), .in_2(button_1_out));
  Counter #(.width(4), .max('hf)) counter_1 (
    .clr(in_2), .load(PC_LODE), .clk(controlled_buffer_1_out), .D(controlled_buffer_5_out), .Q(pgmctr));  // open: up, count, carry
  assign controlled_buffer_1_out = PC_WE ? clk : 1'bz;  // Controlled_Buffer controlled_buffer_1
  Register register_1 (.D(controlled_buffer_2_out), .en(AR_WE), .clk(clk), .Q(register_1_q), .clr(in_2));
  Register register_2 (.D(controlled_buffer_2_out), .en(BR_WE), .clk(clk), .Q(register_2_q), .clr(in_2));
  assign controlled_buffer_2_out = AR_OE ? register_1_q : 8'bz;  // Controlled_Buffer controlled_buffer_2
  ALU8BIT alu8bit_1 (
    .in_3(INV_A), .in_4(INV_B), .in_5(cin), .in_6(SUM), .in_7(AND), .in_8(OR), .out_11(alu8bit_1_out_11[0]),
    .out_12(alu8bit_1_out_11[1]), .in_1(register_1_q), .in_2(register_2_q), .out_13(alu8bit_1_out_13));  // open: out_9, out_10
  Register #(.width(2)) register_3 (.D(alu8bit_1_out_11), .en(FLG_WE), .clk(clk), .Q(FLGR_O), .clr(in_2));
  Register register_4 (.D(alu8bit_1_out_13), .en(ER_WE), .clk(clk), .Q(register_4_q), .clr(in_2));
  Register IR (.D(controlled_buffer_2_out), .en(IR_WE), .clk(clk), .Q(IR_q));  // open: clr
  assign controlled_buffer_2_out = BR_OE ? register_2_q : 8'bz;  // Controlled_Buffer controlled_buffer_3
  assign controlled_buffer_2_out = PC_OE ? {4'b0000, pgmctr} : 8'bz;  // Controlled_Buffer controlled_buffer_4
  assign {controlled_buffer_5_out_2, controlled_buffer_5_out} = PC_LODE ? controlled_buffer_2_out : 8'bz;  // Controlled_Buffer controlled_buffer_5
  assign controlled_buffer_2_out = ER_OE ? register_4_q : 8'bz;  // Controlled_Buffer controlled_buffer_6
  assign controlled_buffer_2_out = IR_OE ? IR_q : 8'bz;  // Controlled_Buffer controlled_buffer_7
  // Probe on controlled_buffer_2_out
  Register register_5 (.D(controlled_buffer_2_out), .en(OUT_WE), .clk(clk), .Q(register_5_q), .clr(in_2));
  assign controlled_buffer_2_out[3:0] = MAR_OB ? register_6_q : 4'bz;  // Controlled_Buffer controlled_buffer_8
  assign controlled_buffer_2_out[7:4] = MAR_OB ? 4'b0000 : 4'bz;  // Controlled_Buffer controlled_buffer_9
  Register #(.width(4)) OPCODE_REG (
    .D(controlled_buffer_2_out[7:4]), .en(OPR_WE), .clk(clk), .Q(OPCODE_REG_q), .clr(in_2));
  assign controlled_buffer_2_out = RAM_OE ? ram_1_dout : 8'bz;  // Controlled_Buffer controlled_buffer_10
  Register #(.width(4)) register_6 (
    .D(controlled_buffer_2_out[3:0]), .en(MAR_WE), .clk(clk), .Q(register_6_q), .clr(in_2));
  _7_Segment_Display u_7_segment_display_1 (
    .g(disp_board_1_out_2), .f(disp_board_1_out_3), .a(disp_board_1_out_4), .b(disp_board_1_out_5),
    .e(disp_board_1_out_14), .d(disp_board_1_out_15), .c(disp_board_1_out_16), .dp(disp_board_1_out_17));
  _7_Segment_Display u_7_segment_display_2 (
    .g(disp_board_1_out_10), .f(disp_board_1_out_11), .a(disp_board_1_out_12), .b(disp_board_1_out_13),
    .e(disp_board_1_out_22), .d(disp_board_1_out_23), .c(disp_board_1_out_24), .dp(disp_board_1_out_25));
  _7_Segment_Display u_7_segment_display_3 (
    .g(disp_board_1_out_6), .f(disp_board_1_out_7), .a(disp_board_1_out_8), .b(disp_board_1_out_9),
    .e(disp_board_1_out_18), .d(disp_board_1_out_19), .c(disp_board_1_out_20), .dp(disp_board_1_out_21));
  assign controlled_buffer_11_out = MAR_OE ? register_6_q : 4'bz;  // Controlled_Buffer controlled_buffer_11
  DISP_BOARD disp_board_1 (
    .in_1(register_5_q), .out_2(disp_board_1_out_2), .out_3(disp_board_1_out_3), .out_4(disp_board_1_out_4),
    .out_5(disp_board_1_out_5), .out_6(disp_board_1_out_6), .out_7(disp_board_1_out_7),
    .out_8(disp_board_1_out_8), .out_9(disp_board_1_out_9), .out_10(disp_board_1_out_10),
    .out_11(disp_board_1_out_11), .out_12(disp_board_1_out_12), .out_13(disp_board_1_out_13),
    .out_14(disp_board_1_out_14), .out_15(disp_board_1_out_15), .out_16(disp_board_1_out_16),
    .out_17(disp_board_1_out_17), .out_18(disp_board_1_out_18), .out_19(disp_board_1_out_19),
    .out_20(disp_board_1_out_20), .out_21(disp_board_1_out_21), .out_22(disp_board_1_out_22),
    .out_23(disp_board_1_out_23), .out_24(disp_board_1_out_24), .out_25(disp_board_1_out_25));
  buf buffer_1 (buffer_1_out, clk);
  // Probe on controlled_buffer_2_out
  // Probe on register_1_q
  // Probe on register_2_q
  // Probe on register_6_q
  RAM #(.addrWidth(4), .databus("bibus")) ram_1 (
    .addr(controlled_buffer_11_out), .we(RAM_WE), .oe(RAM_OE), .clk(clk), .din(controlled_buffer_2_out),
    .dout(ram_1_dout));
  Counter #(.width(3), .max('h7)) counter_2 (
    .clr(in_2), .clk(buffer_1_out), .Q(counter_2_q));  // open: load, up, count, D, carry
  // Probe on pgmctr
  // Probe on OPCODE_REG_q
  // Probe on OPR_WE
  ROM #(.addrWidth(9), .dataWidth(32)) rom_1 (
    .addr({FLGR_O, OPCODE_REG_q, counter_2_q}),
    .data({HLT, OPR_WE, rom_1_data, MAR_OB, OUT_WE, MAR_OE, MAR_WE, RAM_WE, RAM_OE, BR_OE, BR_WE, ER_OE, ER_WE, FLG_OE, FLG_WE, OR, AND, SUM, cin, INV_B, INV_A, AR_OE, AR_WE, PC_OE, PC_WE, PC_LODE, IR_WE, IR_OE}));

  // Other names for the same wires on the sheet: RST = in_2

  // Notes on the sheet:
  //   7.JZ 7
  //   9.AND 9
  //   10.OR A
  //   0.LDA 0
  //   1.LDB 1
  //   2.STA 2
  //   3.STB 3
  //   4.ADD 4
  //   5.SUB 5
  //   6.JMP 6
  //   8.JNZ 8
  //   11. STAL B
  //   13. STAH C
  //   14.HLT F
  //   A REGISTER
  //   PROGRAM COUNTER
  //   ALU
  //   B REGISTER
  //   FLAG REGISTER
  //   E REGISTER
  //   MAR REGISTER
  //   bus
  //   A
  //   B
  //   MAR
  //   RAM
  //   contents of rom_1 (hex, n*v repeats v):
  //   200010 400000 80002 40200009 400000 80020 0 0 200010 400000 80002 40200009 400000 a0000 0 0 200010
  //   400000 80002 40200009 400000 500040 0 0 200010 400000 80002 40600009 400000 100040 0 0 200010 400000
  //   80002 40200009 a400 10020 0 0 200010 400000 80002 40200009 a700 10020 0 0 200010 400000 80002
  //   40200009 d 0 0 0 200010 400000 80002 40200009 4*0 200010 400000 80002 40200009 400000 880000 0 0
  //   200010 400000 80002 40200009 a800 10020 0 0 200010 400000 80002 40200009 4*0 200010 400000 80002
  //   40200009 1000020 0 0 0 200010 400000 80002 40200009 1020000 0 0 0 200010 400000 80002 40200009 4*0
  //   200010 400000 80002 40200009 4*0 8*80000000 200010 400000 80002 40200009 400000 80020 0 0 200010
  //   400000 80002 40200009 400000 a0000 0 0 200010 400000 80002 40200009 400000 500040 0 0 200010 400000
  //   80002 40600009 400000 100040 0 0 200010 400000 80002 40200009 a400 10020 0 0 200010 400000 80002
  //   40200009 a700 10020 0 0 200010 400000 80002 40200009 d 0 0 0 200010 400000 80002 40200009 4*0 200010
  //   400000 80002 40200009 400000 880000 0 0 200010 400000 80002 40200009 a800 10020 0 0 200010 400000
  //   80002 40200009 4*0 200010 400000 80002 40200009 1000020 0 0 0 200010 400000 80002 40200009 1020000 0
  //   0 0 200010 400000 80002 40200009 4*0 200010 400000 80002 40200009 d 0 0 0 8*80000000 200010 400000
  //   80002 40200009 400000 80020 0 0 200010 400000 80002 40200009 400000 a0000 0 0 200010 400000 80002
  //   40200009 400000 500040 0 0 200010 400000 80002 40600009 400000 100040 0 0 200010 400000 80002
  //   40200009 a400 10020 0 0 200010 400000 80002 40200009 a700 10020 0 0 200010 400000 80002 40200009 d 0
  //   0 0 200010 400000 80002 40200009 d 0 0 0 200010 400000 80002 40200009 400000 880000 0 0 200010
  //   400000 80002 40200009 a800 10020 0 0 200010 400000 80002 40200009 4*0 200010 400000 80002 40200009
  //   1000020 0 0 0 200010 400000 80002 40200009 1020000 0 0 0 200010 400000 80002 40200009 4*0 200010
  //   400000 80002 40200009 4*0 8*80000000 200010 400000 80002 40200009 400000 80020 0 0 200010 400000
  //   80002 40200009 400000 a0000 0 0 200010 400000 80002 40200009 400000 500040 0 0 200010 400000 80002
  //   40600009 400000 100040 0 0 200010 400000 80002 40200009 a400 10020 0 0 200010 400000 80002 40200009
  //   a700 10020 0 0 200010 400000 80002 40200009 d 0 0 0 200010 400000 80002 40200009 d 0 0 0 200010
  //   400000 80002 40200009 400000 880000 0 0 200010 400000 80002 40200009 a800 10020 0 0 200010 400000
  //   80002 40200009 4*0 200010 400000 80002 40200009 1000020 0 0 0 200010 400000 80002 40200009 1020000 0
  //   0 0 200010 400000 80002 40200009 4*0 200010 400000 80002 40200009 d 0 0 0 8*80000000
  //   CONTROL UNIT
endmodule

module Clock (
  input  in_1,
  input  in_2,
  input  in_3,
  output out_4
);

  wire and_1_out, and_2_out, clock_1_out, not_1_out, or_1_out;

  Clock_part clock_1 (.out(clock_1_out));
  not not_1 (not_1_out, in_3);
  and and_1 (and_1_out, clock_1_out, ~in_1);  // AND_Gate
  and and_2 (and_2_out, in_1, in_2);
  or or_1 (or_1_out, and_1_out, and_2_out);
  and and_3 (out_4, or_1_out, not_1_out);
endmodule

module DISPLAY_LAYOUT (
  input  [3:0] in_1,
  output out_2,
  output out_3,
  output out_4,
  output out_5,
  output out_6,
  output out_7,
  output out_8,
  output out_9
);

  ROM #(.addrWidth(4)) rom_1 (.addr(in_1), .data({out_9, out_8, out_7, out_6, out_2, out_3, out_4, out_5}));

  // Notes on the sheet:
  //   contents of rom_1 (hex, n*v repeats v):
  //   77 41 3b 6b 4d 6e 7e 43 7f 6f 5f 7c 36 79 3e 1e
endmodule

module BIN_X_DEC (
  input  [7:0] in_1,
  output [3:0] out_2,
  output [3:0] out_3,
  output [3:0] out_4
);

  wire [7:0] divider_1_out;
  wire [7:4] divider_1_rem;

  Divider divider_1 (.a(in_1), .b(8'ha), .out(divider_1_out), .rem({divider_1_rem, out_4}));  // open: upper
  Divider #(.width(4)) divider_2 (
    .a(divider_1_out[3:0]), .b(4'b1010), .out(out_2), .upper(divider_1_out[7:4]), .rem(out_3));
endmodule

module DISP_BOARD (
  input  [7:0] in_1,
  output out_2,
  output out_3,
  output out_4,
  output out_5,
  output out_6,
  output out_7,
  output out_8,
  output out_9,
  output out_10,
  output out_11,
  output out_12,
  output out_13,
  output out_14,
  output out_15,
  output out_16,
  output out_17,
  output out_18,
  output out_19,
  output out_20,
  output out_21,
  output out_22,
  output out_23,
  output out_24,
  output out_25
);

  wire [3:0] bin_x_dec_1_out_2, bin_x_dec_1_out_3, bin_x_dec_1_out_4;

  BIN_X_DEC bin_x_dec_1 (.in_1(in_1), .out_2(bin_x_dec_1_out_2), .out_3(bin_x_dec_1_out_3), .out_4(bin_x_dec_1_out_4));
  DISPLAY_LAYOUT display_layout_1 (
    .in_1(bin_x_dec_1_out_2), .out_6(out_14), .out_7(out_15), .out_8(out_16), .out_9(out_17), .out_2(out_2),
    .out_3(out_3), .out_4(out_4), .out_5(out_5));
  DISPLAY_LAYOUT display_layout_2 (
    .in_1(bin_x_dec_1_out_3), .out_6(out_18), .out_7(out_19), .out_8(out_20), .out_9(out_21), .out_2(out_6),
    .out_3(out_7), .out_4(out_8), .out_5(out_9));
  DISPLAY_LAYOUT display_layout_3 (
    .in_1(bin_x_dec_1_out_4), .out_6(out_22), .out_7(out_23), .out_8(out_24), .out_9(out_25), .out_2(out_10),
    .out_3(out_11), .out_4(out_12), .out_5(out_13));
endmodule
